# Fritzing sketch Fridge (saved by Fritzing 0.9.3b)
perfboards: 1

parts:
  Gizwits_WiFi_Witty_ESP-12F1 = Gizwits WiFi Witty ESP-12F  # not connected
  U1 = Nokia 6100 Color LCD [package=nokia6100_lcd]  # not connected
  2_Channel_Relay1 = 2 Channel Power Relay  # not connected
  DS1 = DS18B20 1-Wire Temperature Sensor Probe Cable  # not connected
  DS2 = DS18B20 1-Wire Temperature Sensor Probe Cable  # not connected
  DS3 = DS18B20 1-Wire Temperature Sensor Probe Cable  # not connected
  J11 = JST-03JQ-BT [part_number=JST-JQ-BT package=THT]
  J3 = female pin header, 8 pins [form="♀ (female)"]
  J13 = JST-03JQ-BT [part_number=JST-JQ-BT package=THT]
  J2 = female pin header, 8 pins [form="♀ (female)"]
  J6 = Screw terminal - 2 pins [package=THT]
  R1 = Resistor [tolerance=±5% resistance=4.7k package="0402 [SMD]"]
  J7 = Screw terminal - 2 pins [package=THT]
  J15 = JST-03JQ-BT [part_number=JST-JQ-BT package=THT]
  J17 = JST-03JQ-BT [part_number=JST-JQ-BT package=THT]

nets:
  N1: J11.pin2, J3.pin5, J13.pin2, R1.Pin_1, J15.pin2, J17.pin2
  N2: J11.pin1, J3.pin1, J13.pin1, J6.pin2, J15.pin1, J17.pin1
  N3: J11.pin3, J13.pin3, J2.pin1, R1.Pin_0, J7.pin1, J15.pin3, J17.pin3
  N4: J2.pin4, J6.pin1
  N5: J2.pin5, J7.pin2

custom parts:
  2 Channel Power Relay: A 2 channel power relay. The module operates at 5V.
